# Fritzing sketch SmallKat (saved by Fritzing 0.9.2b)
circuit board: 8.5cm x 5.64cm
perfboards: 1

parts:
  ESP32_1_bd = female pin header, 19 pins [form="♀ (female)"]
  ESP32_2_bd = female pin header, 19 pins [form="♀ (female)"]
  ESP32-BDExt-1 = female pin header, 19 pins [form="♀ (female)"]
  ESP32-BDExt-2 = female pin header, 19 pins [form="♀ (female)"]
  GND_1a = male pin header, 12 pins [form="♂ (male)"]
  GND_1b = male pin header, 4 pins [form="♂ (male)"]
  5V_1a = male pin header, 12 pins [form="♂ (male)"]
  Sig_Rail_1a = male pin header, 12 pins [form="♂ (male)"]
  5V_1b = male pin header, 4 pins [form="♂ (male)"]
  Sig_1b = male pin header, 4 pins [form="♂ (male)"]
  GND_2b = male pin header, 12 pins [form="♂ (male)"]
  GND_2a = male pin header, 5 pins [form="♂ (male)"]
  5V_2b = male pin header, 12 pins [form="♂ (male)"]
  Sig_2b = male pin header, 12 pins [form="♂ (male)"]
  5V_2a = male pin header, 5 pins [form="♂ (male)"]
  Sig_2a = male pin header, 5 pins [form="♂ (male)"]
  XT60-BAT_In = XT60 Connector [package=THT]
  GND_Ex = male pin header, 5 pins [form="♂ (male)"]
  5V_Ex = male pin header, 5 pins [form="♂ (male)"]
  BEC_1 = male pin header, 3 pins [form="♂ (male)"]
  BEC_2 = male pin header, 3 pins [form="♂ (male)"]
  BEC_3 = male pin header, 3 pins [form="♂ (male)"]
  Fz_Sw_VIn = male pin header, 5 pins [form="♂ (male)"]
  BNO055 = male pin header, 6 pins [form="♂ (male)"]
  BNO55_rear = male pin header, 4 pins [form="♂ (male)"]  # not connected

nets:
  N1: ESP32_1_bd.pin1, ESP32-BDExt-1.pin1, 5V_Ex.pin1, 5V_Ex.pin2, 5V_Ex.pin3, 5V_Ex.pin4, 5V_Ex.pin5, BEC_2.pin2, BNO055.pin1
  N2: ESP32_1_bd.pin2, ESP32-BDExt-1.pin2, Sig_1b.pin1
  N3: ESP32_1_bd.pin3, ESP32-BDExt-1.pin3, Sig_1b.pin2
  N4: ESP32_1_bd.pin4, ESP32-BDExt-1.pin4, Sig_1b.pin3
  N5: ESP32_1_bd.pin5, ESP32-BDExt-1.pin5, Sig_1b.pin4
  N6: ESP32_1_bd.pin6, ESP32-BDExt-1.pin6
  N7: ESP32_1_bd.pin7, ESP32-BDExt-1.pin7, Sig_Rail_1a.pin1
  N8: ESP32_1_bd.pin8, ESP32-BDExt-1.pin8, Sig_Rail_1a.pin2
  N9: ESP32_1_bd.pin9, ESP32-BDExt-1.pin9, Sig_Rail_1a.pin3
  N10: ESP32_1_bd.pin10, ESP32-BDExt-1.pin10, Sig_Rail_1a.pin4
  N11: ESP32_1_bd.pin11, ESP32-BDExt-1.pin11, Sig_Rail_1a.pin5
  N12: ESP32_1_bd.pin12, ESP32-BDExt-1.pin12, Sig_Rail_1a.pin6
  N13: ESP32_1_bd.pin13, ESP32-BDExt-1.pin13, Sig_Rail_1a.pin7
  N14: ESP32_1_bd.pin14, ESP32-BDExt-1.pin14, Sig_Rail_1a.pin8
  N15: ESP32_1_bd.pin15, ESP32-BDExt-1.pin15, Sig_Rail_1a.pin9
  N16: ESP32_1_bd.pin16, ESP32-BDExt-1.pin16, Sig_Rail_1a.pin10
  N17: ESP32_1_bd.pin17, ESP32-BDExt-1.pin17, Sig_Rail_1a.pin11
  N18: ESP32_1_bd.pin18, ESP32-BDExt-1.pin18, Sig_Rail_1a.pin12
  N19: ESP32_1_bd.pin19, ESP32-BDExt-1.pin19
  N20: ESP32_2_bd.pin1, ESP32-BDExt-2.pin1, Sig_2b.pin1
  N21: ESP32_2_bd.pin2, ESP32-BDExt-2.pin2, Sig_2b.pin2
  N22: ESP32_2_bd.pin3, ESP32-BDExt-2.pin3, Sig_2b.pin3
  N23: ESP32_2_bd.pin4, ESP32-BDExt-2.pin4, Sig_2b.pin4
  N24: ESP32_2_bd.pin5, ESP32-BDExt-2.pin5, Sig_2b.pin5
  N25: ESP32_2_bd.pin6, ESP32-BDExt-2.pin6, Sig_2b.pin6
  N26: ESP32_2_bd.pin7, ESP32-BDExt-2.pin7, Sig_2b.pin7
  N27: ESP32_2_bd.pin8, ESP32-BDExt-2.pin8, Sig_2b.pin8
  N28: ESP32_2_bd.pin9, ESP32-BDExt-2.pin9, Sig_2b.pin9
  N29: ESP32_2_bd.pin10, ESP32-BDExt-2.pin10, Sig_2b.pin10
  N30: ESP32_2_bd.pin11, ESP32-BDExt-2.pin11, Sig_2b.pin11
  N31: ESP32_2_bd.pin12, ESP32-BDExt-2.pin12, Sig_2b.pin12
  N32: ESP32_2_bd.pin13, ESP32-BDExt-2.pin13
  N33: ESP32_2_bd.pin14, ESP32-BDExt-2.pin14, Sig_2a.pin1
  N34: ESP32_2_bd.pin15, ESP32-BDExt-2.pin15, Sig_2a.pin2
  N35: ESP32_2_bd.pin16, ESP32-BDExt-2.pin16, Sig_2a.pin3
  N36: ESP32_2_bd.pin17, ESP32-BDExt-2.pin17, Sig_2a.pin4
  N37: ESP32_2_bd.pin18, ESP32-BDExt-2.pin18, Sig_2a.pin5
  N38: ESP32_2_bd.pin19, ESP32-BDExt-2.pin19, GND_1a.pin1, GND_1a.pin2, GND_1a.pin3, GND_1a.pin4, GND_1a.pin5, GND_1a.pin6, GND_1a.pin7, GND_1a.pin8, GND_1a.pin9, GND_1a.pin10, GND_1a.pin11, GND_1a.pin12, GND_1b.pin1, GND_1b.pin2, GND_1b.pin3, GND_1b.pin4, GND_2b.pin1, GND_2b.pin2, GND_2b.pin3, GND_2b.pin4, GND_2b.pin5, GND_2b.pin6, GND_2b.pin7, GND_2b.pin8, GND_2b.pin9, GND_2b.pin10, GND_2b.pin11, GND_2b.pin12, GND_2a.pin1, GND_2a.pin2, GND_2a.pin3, GND_2a.pin4, GND_2a.pin5, XT60-BAT_In.GND, GND_Ex.pin1, GND_Ex.pin2, GND_Ex.pin3, GND_Ex.pin4, GND_Ex.pin5, BEC_1.pin1, BEC_2.pin1, BEC_3.pin3, BNO055.pin3
  N39: 5V_1a.pin1, 5V_1a.pin2, 5V_1a.pin3, 5V_1a.pin4, 5V_1a.pin5, 5V_1a.pin6, 5V_1a.pin7, 5V_1a.pin8, 5V_1a.pin9, 5V_1a.pin10, 5V_1a.pin11, 5V_1a.pin12, 5V_1b.pin1, 5V_1b.pin2, 5V_1b.pin3, 5V_1b.pin4, BEC_1.pin2
  N40: 5V_2b.pin1, 5V_2b.pin2, 5V_2b.pin3, 5V_2b.pin4, 5V_2b.pin5, 5V_2b.pin6, 5V_2b.pin7, 5V_2b.pin8, 5V_2b.pin9, 5V_2b.pin10, 5V_2b.pin11, 5V_2b.pin12, 5V_2a.pin1, 5V_2a.pin2, 5V_2a.pin3, 5V_2a.pin4, 5V_2a.pin5, BEC_3.pin2
  N41: XT60-BAT_In.VCC, Fz_Sw_VIn.pin1

notes:
  USB end
  Parts to add:
  xSwitch, xFuse,
  x5V&Gnd pins,
  xWakeup

custom parts:
  XT60 Connector: Yellow XT60 connector for high current loads up to 40A
